# Fritzing sketch project2Fritzing (saved by Fritzing 0.9.3b)
stripboards: 1

parts:
  M2 = DC Motor
  VCC1 = 4 x AAA Battery Mount
  M1 = DC Motor
  U6 = TCM8240MD [package=tcm8240md]  # not connected
  MCU1 = Raspberry Pi B+  # not connected
  U7 = TCRT5000 [package=THT]
  U8 = TCRT5000 [package=THT]
  U9 = TCRT5000 [package=THT]
  U10 = TCRT5000 [package=THT]
  Part1 = Adafruit DC+Stepper Motor HAT [part_number="Adafruit #2348"]
  R1 = Resistor [tolerance=±5% resistance=100 package="0805 [SMD]"]
  R2 = Resistor [tolerance=±5% resistance=100 package="0805 [SMD]"]
  R3 = Resistor [tolerance=±5% resistance=100 package="0805 [SMD]"]
  R4 = Resistor [tolerance=±5% resistance=100 package="0805 [SMD]"]
  R5 = Resistor [tolerance=±5% resistance=4.7k package="0805 [SMD]"]
  R6 = Resistor [tolerance=±5% resistance=4.7k package="0805 [SMD]"]
  R7 = Resistor [tolerance=±5% resistance=4.7k package="0805 [SMD]"]
  R8 = Resistor [tolerance=±5% resistance=4.7k package="0805 [SMD]"]
  U11 = HC-SR04 [chip_label=IC package="SIP (Single Inline) [THT]"]
  Part2 = Adafruit 3.5in 480x320 TFT FeatherWing [part_number="Adafrruit #3651"]  # not connected

nets:
  N1: M2.pin_1, Part1.M2A
  N2: M2.pin_2, Part1.M2B
  GND: VCC1.-, U10.Pin_1, Part1.GND, R8.Pin_0, U11.GND
  N3: VCC1.+, Part1.VMOTOR
  N4: M1.pin_1, Part1.M1B
  N5: M1.pin_2, Part1.M1A
  N6: U7.Pin_1, Part1.GPIO16, R7.Pin_1
  N7: U7.Pin_2, U7.Pin_3, U8.Pin_2, U8.Pin_3, U9.Pin_2, U9.Pin_3, Part1.GPIO12
  N8: U7.Pin_4, R2.Pin_1
  N9: U8.Pin_1, Part1.GPIO21, R5.Pin_1
  N10: U8.Pin_4, R4.Pin_1
  N11: U9.Pin_1, Part1.GPIO20, R6.Pin_1
  N12: U9.Pin_4, R3.Pin_1
  N13: U10.Pin_4, R1.Pin_1
  N14: Part1.5.0V, R1.Pin_0, R2.Pin_0, R3.Pin_0, R4.Pin_0, R5.Pin_0, R6.Pin_0, R7.Pin_0, R8.Pin_1, U11.Vcc
  N15: Part1.GPIO19, U11.Echo
  N16: Part1.GPIO26, U11.Trig

custom parts:
  TCRT5000: TCRT5000 optical reflective sensor
  Adafruit DC+Stepper Motor HAT: Let your robotic dreams come true with the new DC+Stepper Motor HAT from Adafruit. This Raspberry Pi add-on is perfect for any motion project as it can drive up to 4 DC or 2 Stepper motors with full PWM speed control. Since the Raspberry Pi does not have a lot of PWM pins, we use a fully-dedicated PWM driver chip onboard to both control motor direction and speed. This chip handles all the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
  HC-SR04: HC-SR04 ultrasound distance sensor
  Adafruit 3.5in 480x320 TFT FeatherWing: Spice up your Feather project with a beautiful 3.5" touchscreen display shield with built in microSD card socket. This TFT display is 3.5" diagonal with a bright 6 white-LED backlight. You get a massive 480x320 pixels with individual 16-bit color pixel control. It has way more resolution than a black and white 128x64 display, and twice as much as our 2.4" TFT FeatherWing. As a bonus, this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
